# Fritzing sketch Shield (saved by Fritzing 0.8.5b)
circuit board: 10.16cm x 5.36194cm
breadboards: 1

parts:
  Part1 = Arduino Due (Rev2b)
  T1 = TMP36 Temperature Sensor [package="TO92 [THT]"]
  T2 = TMP36 Temperature Sensor [package="TO92 [THT]"]
  U1 = SD_CARD_SOCKET [package=sdcard_4uconn]  # not connected

nets:
  N1: Part1.A2, T1.Vout
  N2: Part1.A3, T2.Vout
  N3: Part1.IOREF, T1.+Vs, T2.+Vs
  GND: Part1.GND, T1.GND, T2.GND
